# Fritzing sketch nail2nail (saved by Fritzing 0.9.2b)
breadboards: 1

parts:
  Part1 = Arduino Uno (Rev3)
  R1 = Resistor [tolerance=±5% resistance=220 package=THT]
  ANT1 = Antenna
  ANT2 = Antenna
  R2 = Resistor [tolerance=±20% resistance=4.7k package="0402 [SMD]"]
  U2 = AD22100 - Voltage Output Temperature Sensor with Signal Conditioning [part_number=AD22100]
  pH_Circuit1 = pH Circuit
  U3 = BNC [package=bnc]
  KY-1 = Keyes Relay [package=THT]  # not connected

nets:
  N1: Part1.A0, R1.Pin_1, ANT1.antenna_lead
  N2: Part1.A4/SDA, pH_Circuit1.TX
  N3: Part1.A5/SCL, pH_Circuit1.RX
  N4: Part1.D12/MISO, R1.Pin_0
  N5: Part1.D13/SCK, ANT2.antenna_lead
  N6: Part1.D3_PWM, R2.Pin_1, U2.GND
  3V3: Part1.3V3, R2.Pin_0, U2.V+, pH_Circuit1.Vcc
  N7: Part1.GND, U2.Vo, pH_Circuit1.GND#0
  N8: pH_Circuit1.PRB, U3.OUT
  N9: pH_Circuit1.GND#5, U3.GND

custom parts:
  Keyes Relay: The Keyes 5V relay module is suitable for SCM development, home appliance control. It uses a 5V~12V TIL control signal which can control DC / AC signal.
